// Digital circuit IF-ID.dig as structural Verilog
module IF_ID (
  input  [31:0] pc_in,
  input  [31:0] inst_in,
  input  clk,
  input  rst,
  output [31:0] pc_out,
  output [31:0] inst_out
);

  IF_ID #(.applicationType("IVERILOG")) u_IF_ID (
    .clk(clk), .rst(rst), .pc_in(pc_in), .inst_in(inst_in), .pc_out(pc_out), .inst_out(inst_out));
endmodule

/* Code of IF_ID:
module IF_ID(clk, rst, pc_in, inst_in, pc_out, inst_out);
	input clk, rst;
	input [31:0] pc_in, inst_in;
	output [31:0] pc_out, inst_out;
	
	reg [31:0] pc_out, inst_out;
	
	always @(posedge clk)
	begin
		if (rst)
		begin
			pc_out = 0;
			inst_out = 0;
		end
		else 
		begin
			pc_out = pc_in;
			inst_out = inst_in;
		end
	end

endmodule
*/
