// Digital circuit code.dig as structural Verilog
// 根据指令前8位的地址，取出完整32位指令
module code (
  input  [31:0] pc,
  output [31:0] inst
);

  ROM #(.AddrBits(20), .Bits(32)) rom_1 (.A(pc[21:2]), .sel(1'b1), .D(inst));

  // Notes on the sheet:
  //   pc: 指令地址
  //   rom_1 loads comprehensive_test.hex
endmodule
