// Digital circuit forwarding_unit.dig as structural Verilog
module forwarding_unit (
  input  [31:0] rs1_IDEX,
  input  [31:0] rs2_IDEX,
  input  write_EXMEM,
  input  [4:0] rd_EXMEM,
  input  write_MEMWB,
  input  [4:0] rd_MEMWB,
  output [1:0] forward_A,
  output [1:0] forward_B
);

  forwarding_unit #(.applicationType("IVERILOG")) u_forwarding_unit (
    .rs1_IDEX(rs1_IDEX), .rs2_IDEX(rs2_IDEX), .write_EXMEM(write_EXMEM), .rd_EXMEM(rd_EXMEM),
    .write_MEMWB(write_MEMWB), .rd_MEMWB(rd_MEMWB), .forward_A(forward_A), .forward_B(forward_B));
endmodule

/* Code of forwarding_unit:
module forwarding_unit(rs1_IDEX, rs2_IDEX, write_EXMEM, rd_EXMEM, 
	write_MEMWB, rd_MEMWB,
	forward_A, forward_B);
	
	input [31:0] rs1_IDEX, rs2_IDEX;
	input write_EXMEM;
	input [4:0] rd_EXMEM; 
	input write_MEMWB;
	input [4:0] rd_MEMWB;
	output [1:0] forward_A, forward_B;
	
	assign forward_A = (write_EXMEM && rd_EXMEM != 0 && rd_EXMEM == rs1_IDEX) ? 10 :
			   (write_MEMWB && rd_MEMWB != 0 && rd_MEMWB == rs1_IDEX) ? 01 : 00;

	assign forward_B = (write_EXMEM && rd_EXMEM != 0 && rd_EXMEM == rs2_IDEX) ? 10 :
			   (write_MEMWB && rd_MEMWB != 0 && rd_MEMWB == rs2_IDEX) ? 01 : 00;
	
endmodule
*/
