// Digital circuit main.dig as structural Verilog
module main (
  input  rst,
  input  clk
);

  wire and_1_out, cmp_1_out, controller_1_pc_in_sel, controller_1_pc_load, controller_1_r1_pc_sel,
       controller_1_r2_imm_sel, controller_1_rf_write, ex_mem_1_cmp_result_out, ex_mem_1_pc_in_sel_out,
       ex_mem_1_pc_load_out, ex_mem_1_rf_write_out, id_ex_1_p27, id_ex_1_p28, id_ex_1_p29, id_ex_1_p30,
       id_ex_1_p31, mem_wb_1_rf_write_out;
  wire [1:0] controller_1_rf_in_sel, ex_mem_1_rf_in_sel_out, forwarding_unit_1_forward_a,
       forwarding_unit_1_forward_b, id_ex_1_p32, mem_wb_1_rf_in_sel_out;
  wire [2:0] controller_1_lu_op, id_ex_1_p26;
  wire [3:0] controller_1_alu_op, controller_1_memory_op, ex_mem_1_memory_op_out, id_ex_1_p24, id_ex_1_p25;
  wire [4:0] decode_1_rd, decode_1_rs1, decode_1_rs2, ex_mem_1_rd_out, id_ex_1_p22, id_ex_1_p33, id_ex_1_p34,
       mem_wb_1_rd_out;
  wire [6:0] decode_1_opcode;
  wire [9:0] decode_1_funct;
  wire [31:0] add_1_s, alu_1_out, code_1_inst, decode_1_imm, ex_mem_1_alu_result_out, ex_mem_1_pc_out,
       ex_mem_1_r2_out, id_ex_1_p19, id_ex_1_p20, id_ex_1_p21, id_ex_1_p23, if_id_1_inst_out, if_id_1_pc_out,
       mem_wb_1_alu_result_out, mem_wb_1_dout_out, mem_wb_1_pc_out, memory_1_dout, multiplexer_1_out,
       multiplexer_2_out, multiplexer_3_out, multiplexer_4_out, multiplexer_5_out, multiplexer_6_out,
       pc_1_dout, pc_4_1_pc_out, regfile_1_r1, regfile_1_r2;

  Multiplexer #(.Bits(32)) multiplexer_1 (
    .sel(and_1_out), .in_0(pc_4_1_pc_out), .in_1(ex_mem_1_alu_result_out), .out(multiplexer_1_out));
  pc_4 pc_4_1 (.pc_out(pc_4_1_pc_out), .pc(pc_1_dout));
  pc pc_1 (.clk(clk), .rst(rst), .load(ex_mem_1_pc_load_out), .din(multiplexer_1_out), .dout(pc_1_dout));
  code code_1 (.pc(pc_1_dout), .inst(code_1_inst));
  // Probe on code_1_inst
  IF_ID if_id_1 (
    .clk(clk), .rst(rst), .pc_in(pc_1_dout), .inst_in(code_1_inst), .pc_out(if_id_1_pc_out),
    .inst_out(if_id_1_inst_out));
  decode decode_1 (
    .inst(if_id_1_inst_out), .opcode(decode_1_opcode), .funct(decode_1_funct), .rs1(decode_1_rs1),
    .rs2(decode_1_rs2), .rd(decode_1_rd), .imm(decode_1_imm));
  regfile regfile_1 (
    .clk(clk), .rst(rst), .rs1(decode_1_rs1), .rs2(decode_1_rs2), .rd(mem_wb_1_rd_out),
    .write(mem_wb_1_rf_write_out), .din(multiplexer_6_out), .r1(regfile_1_r1), .r2(regfile_1_r2));
  controller controller_1 (
    .memory_op(controller_1_memory_op), .alu_op(controller_1_alu_op), .lu_op(controller_1_lu_op),
    .r1_pc_sel(controller_1_r1_pc_sel), .r2_imm_sel(controller_1_r2_imm_sel), .pc_load(controller_1_pc_load),
    .pc_in_sel(controller_1_pc_in_sel), .rf_write(controller_1_rf_write), .rf_in_sel(controller_1_rf_in_sel),
    .clk(clk), .rst(rst), .opcode(decode_1_opcode), .funct(decode_1_funct));
  // ID_EX id_ex_1: pin names not known; wires that end beside it: clk, rst, if_id_1_pc_out, regfile_1_r1, regfile_1_r2, decode_1_rd, decode_1_imm, controller_1_memory_op, controller_1_alu_op, controller_1_lu_op, controller_1_r1_pc_sel, controller_1_r2_imm_sel, controller_1_pc_load, controller_1_pc_in_sel, controller_1_rf_write, controller_1_rf_in_sel, decode_1_rs1, decode_1_rs2, id_ex_1_p19, id_ex_1_p20, id_ex_1_p21, id_ex_1_p22, id_ex_1_p23, id_ex_1_p24, id_ex_1_p25, id_ex_1_p26, id_ex_1_p27, id_ex_1_p28, id_ex_1_p29, id_ex_1_p30, id_ex_1_p31, id_ex_1_p32, id_ex_1_p33, id_ex_1_p34
  forwarding_unit forwarding_unit_1 (
    .rs1_IDEX(id_ex_1_p33), .rs2_IDEX(id_ex_1_p34), .rd_EXMEM(ex_mem_1_rd_out),
    .write_EXMEM(ex_mem_1_rf_write_out), .rd_MEMWB(mem_wb_1_rd_out), .write_MEMWB(mem_wb_1_rf_write_out),
    .forward_A(forwarding_unit_1_forward_a), .forward_B(forwarding_unit_1_forward_b));
  Multiplexer #(.Bits(32)) multiplexer_2 (
    .sel(id_ex_1_p27), .in_0(id_ex_1_p20), .in_1(id_ex_1_p19), .out(multiplexer_2_out));
  Multiplexer #(.Bits(32)) multiplexer_3 (
    .sel(id_ex_1_p28), .in_0(id_ex_1_p21), .in_1(id_ex_1_p23), .out(multiplexer_3_out));
  Multiplexer #(.Bits(32), .Selector_Bits(2)) multiplexer_4 (
    .sel(forwarding_unit_1_forward_a), .in_0(multiplexer_2_out), .in_1(multiplexer_6_out),
    .in_2(ex_mem_1_alu_result_out), .in_3({32{1'b0}}), .out(multiplexer_4_out));
  Multiplexer #(.Selector_Bits(2), .Bits(32)) multiplexer_5 (
    .sel(forwarding_unit_1_forward_b), .in_0(multiplexer_3_out), .in_1(multiplexer_6_out),
    .in_2(ex_mem_1_alu_result_out), .in_3({32{1'b0}}), .out(multiplexer_5_out));
  cmp cmp_1 (.op(id_ex_1_p26), .in1(id_ex_1_p20), .in2(id_ex_1_p21), .out(cmp_1_out));
  alu alu_1 (.op(id_ex_1_p25), .in1(multiplexer_4_out), .in2(multiplexer_5_out), .out(alu_1_out));
  EX_MEM ex_mem_1 (
    .clk(clk), .rst(rst), .cmp_result(cmp_1_out), .alu_result(alu_1_out), .memory_op(id_ex_1_p24),
    .r2(id_ex_1_p21), .rd(id_ex_1_p22), .rf_write(id_ex_1_p31), .rf_in_sel(id_ex_1_p32), .pc(id_ex_1_p19),
    .pc_load(id_ex_1_p29), .pc_in_sel(id_ex_1_p30), .cmp_result_out(ex_mem_1_cmp_result_out),
    .alu_result_out(ex_mem_1_alu_result_out), .r2_out(ex_mem_1_r2_out),
    .memory_op_out(ex_mem_1_memory_op_out), .rd_out(ex_mem_1_rd_out), .rf_write_out(ex_mem_1_rf_write_out),
    .rf_in_sel_out(ex_mem_1_rf_in_sel_out), .pc_out(ex_mem_1_pc_out), .pc_load_out(ex_mem_1_pc_load_out),
    .pc_in_sel_out(ex_mem_1_pc_in_sel_out));
  and and_1 (and_1_out, ex_mem_1_cmp_result_out, ex_mem_1_pc_in_sel_out);
  Terminal terminal_1 (.D(ex_mem_1_r2_out), .C(clk), .en(ex_mem_1_memory_op_out[3]));
  memory memory_1 (
    .clk(clk), .rst(rst), .address(ex_mem_1_alu_result_out), .din(ex_mem_1_r2_out),
    .op(ex_mem_1_memory_op_out), .dout(memory_1_dout));
  MEM_WB mem_wb_1 (
    .clk(clk), .rst(rst), .rd(ex_mem_1_rd_out), .rf_write(ex_mem_1_rf_write_out),
    .rf_in_sel(ex_mem_1_rf_in_sel_out), .alu_result(ex_mem_1_alu_result_out), .dout(memory_1_dout),
    .pc(ex_mem_1_pc_out), .rd_out(mem_wb_1_rd_out), .rf_write_out(mem_wb_1_rf_write_out),
    .rf_in_sel_out(mem_wb_1_rf_in_sel_out), .alu_result_out(mem_wb_1_alu_result_out),
    .dout_out(mem_wb_1_dout_out), .pc_out(mem_wb_1_pc_out));
  Add #(.Bits(32)) add_1 (.a(mem_wb_1_pc_out), .b(32'h4), .c_i(1'b0), .s(add_1_s));  // open: c_o
  Multiplexer #(.Selector_Bits(2), .Bits(32)) multiplexer_6 (
    .sel(mem_wb_1_rf_in_sel_out), .in_0(mem_wb_1_alu_result_out), .in_1(mem_wb_1_dout_out), .in_2(add_1_s),
    .in_3({32{1'b0}}), .out(multiplexer_6_out));

  // Notes on the sheet:
  //   clk: Hz: 10
endmodule
